# Fritzing sketch Schematic View (Fritzing) (saved by Fritzing 0.9.10b)
breadboards: 1

parts:
  M5Core-Ink1 = M5Core-Ink
  M5Stack-RGB-Unit1 = rgb-led-unit [package=M5Stack]
  S1 = SWITCH-MOMENTARY-2 [package=tactile_switch_smd]

nets:
  N1: M5Core-Ink1.6_G26, S1.2
  GND: M5Core-Ink1.8_GND, S1.1
  N2: M5Core-Ink1.9_GND, M5Stack-RGB-Unit1.GND-A
  N3: M5Core-Ink1.10_5V, M5Stack-RGB-Unit1.5V-A
  N4: M5Core-Ink1.11_G32, M5Stack-RGB-Unit1.OUT-A
  N5: M5Core-Ink1.12_G33, M5Stack-RGB-Unit1.IN-A

custom parts:
  M5Core-Ink: M5Stack Core Ink ESP32 Board
  rgb-led-unit: M5Stack SK6812 RGB LED Unit (U003)
